# Fritzing sketch LightGary (saved by Fritzing 0.9.2b)
breadboards: 2

parts:
  Bauteil1 = Arduino Uno (Rev3)
  SW1 = ENCODER_RGB_CA [package=encoder_led_3]  # not connected
  LED1 = RGB LED - (4 legs) [package="5 mm [THT]"]
  ENCODER1 = Rotary Encoder with Knob  # not connected
  IC1 = MCP23017 I2C I/O Expander  # not connected
  U1 = 74HC595 [package="DIP16 [THT]"]  # not connected
  RTC1 = DS1307 RTC Breakout

nets:
  5V: Bauteil1.5V, LED1.common_anode, RTC1.5V
  GND: Bauteil1.GND, RTC1.GND

custom parts:
  Rotary Encoder with Knob: Rotary Encoder with 1/4" Shaft and Knob
  MCP23017 I2C I/O Expander: The MCP23017 uses two i2c pins (these can be shared with other i2c devices), and in exchange gives you 16 general purpose pins. You can set each of 16 pins to be input, output, input with a pullup or open drain. There's even the ability to get an interrupt via an external pin when any of the inputs change so you don't have to keep polling the chip.
  DS1307 RTC Breakout: DS1307 Real-time Clock Breakout Board with Battery
